// Logisim project carrySelectAdder.circ as structural Verilog
module mx2i_4 (
  input  [3:0] in_1,
  input  [3:0] in_2,
  input  s,
  output [3:0] out_4
);

  twoOneTransmission twoonetransmission_1 (.in_1(in_1[0]), .in_2(in_2[0]), .in_3(s), .out_4(out_4[0]));
  twoOneTransmission twoonetransmission_2 (.in_1(in_1[1]), .in_2(in_2[1]), .in_3(s), .out_4(out_4[1]));
  twoOneTransmission twoonetransmission_3 (.in_1(in_1[2]), .in_2(in_2[2]), .in_3(s), .out_4(out_4[2]));
  twoOneTransmission twoonetransmission_4 (.in_1(in_1[3]), .in_2(in_2[3]), .in_3(s), .out_4(out_4[3]));
endmodule

module eightBitCarry (
  input  [7:0] in_1,
  input  [7:0] in_2,
  output [7:0] _10_5,
  output _10_5_2
);

  wire fourbitone_1__8_00, fourbitzero_1__8_00, fourbitzero_2__8_00, twoonetransmission_1_out_4;
  wire [3:0] fourbitone_1__8_75, fourbitzero_1__8_75, mx2i_4_1_out_4;

  twoOneTransmission twoonetransmission_1 (
    .in_1(fourbitzero_1__8_00), .in_2(fourbitone_1__8_00), .in_3(fourbitzero_2__8_00),
    .out_4(twoonetransmission_1_out_4));
  fourBitOne fourbitone_1 (.a(in_1[7:4]), .b(in_2[7:4]), ._8_00(fourbitone_1__8_00), ._8_75(fourbitone_1__8_75));
  mx2i_4 mx2i_4_1 (
    .in_2(fourbitone_1__8_75), .in_1(fourbitzero_1__8_75), .s(fourbitzero_2__8_00), .out_4(mx2i_4_1_out_4));
  fourBitZero fourbitzero_1 (.a(in_1[7:4]), .b(in_2[7:4]), ._8_00(fourbitzero_1__8_00), ._8_75(fourbitzero_1__8_75));
  fourInverter fourinverter_1 (.in_1(mx2i_4_1_out_4), .out_2(_10_5[7:4]));
  not not_1 (_10_5_2, twoonetransmission_1_out_4);
  fourBitZero fourbitzero_2 (.a(in_1[3:0]), .b(in_2[3:0]), ._8_00(fourbitzero_2__8_00), ._8_75(_10_5[3:0]));

  // Notes on the sheet:
  //   8.00
  //   9.75
  //   8.75
  //   8.00
  //   9.75
  //   8.75
  //   10.5
  //   10.5
  //   8.00
  //   8.75
  //   Eight Bit Carry Select Adder
endmodule

module fourInverter (
  input  [3:0] in_1,
  output [3:0] out_2
);

  not not_1 (out_2[0], in_1[0]);
  not not_2 (out_2[1], in_1[1]);
  not not_3 (out_2[2], in_1[2]);
  not not_4 (out_2[3], in_1[3]);
endmodule

module sixteenBitCarry (
  input  [15:0] in_1,
  input  [15:0] in_2,
  output [15:0] _13,
  output _13_2
);

  wire eightbitcarry_1__10_5_2, eightbitcarry_2__10_5_2, eightbitcarryone_1__10_5_2,
       twoonetransmission_1_out_4;
  wire [7:0] eightbitcarry_1__10_5, eightbitcarryone_1__10_5, mx2i_8_1_out_4;

  eightBitCarryOne eightbitcarryone_1 (
    .in_2(in_2[15:8]), .in_1(in_1[15:8]), ._10_5(eightbitcarryone_1__10_5),
    ._10_5_2(eightbitcarryone_1__10_5_2));
  twoOneTransmission twoonetransmission_1 (
    .in_1(eightbitcarry_1__10_5_2), .in_2(eightbitcarryone_1__10_5_2), .in_3(eightbitcarry_2__10_5_2),
    .out_4(twoonetransmission_1_out_4));
  eightBitCarry eightbitcarry_1 (
    .in_2(in_2[15:8]), .in_1(in_1[15:8]), ._10_5(eightbitcarry_1__10_5), ._10_5_2(eightbitcarry_1__10_5_2));
  mx2i_8 mx2i_8_1 (
    .in_1(eightbitcarry_1__10_5), .in_2(eightbitcarryone_1__10_5), .s(eightbitcarry_2__10_5_2),
    .out_4(mx2i_8_1_out_4));
  not not_1 (_13_2, twoonetransmission_1_out_4);
  eightInverter eightinverter_1 (.in_1(mx2i_8_1_out_4), .out_2(_13[15:8]));
  eightBitCarry eightbitcarry_2 (
    .in_2(in_2[7:0]), .in_1(in_1[7:0]), ._10_5(_13[7:0]), ._10_5_2(eightbitcarry_2__10_5_2));

  // Notes on the sheet:
  //   10.5
  //   10.5
  //   12.25
  //   10.5
  //   10.5
  //   12.25
  //   10.5
  //   13
  //   10.5
endmodule

module eightBitCarryOne (
  input  [7:0] in_1,
  input  [7:0] in_2,
  output [7:0] _10_5,
  output _10_5_2
);

  wire fourbitone_1__8_00, fourbitone_2__8_00, fourbitzero_1__8_00, twoonetransmission_1_out_4;
  wire [3:0] fourbitone_1__8_75, fourbitzero_1__8_75, mx2i_4_1_out_4;

  twoOneTransmission twoonetransmission_1 (
    .in_1(fourbitzero_1__8_00), .in_2(fourbitone_1__8_00), .in_3(fourbitone_2__8_00),
    .out_4(twoonetransmission_1_out_4));
  fourBitOne fourbitone_1 (.a(in_1[7:4]), .b(in_2[7:4]), ._8_00(fourbitone_1__8_00), ._8_75(fourbitone_1__8_75));
  mx2i_4 mx2i_4_1 (
    .in_2(fourbitone_1__8_75), .in_1(fourbitzero_1__8_75), .s(fourbitone_2__8_00), .out_4(mx2i_4_1_out_4));
  fourBitZero fourbitzero_1 (.a(in_1[7:4]), .b(in_2[7:4]), ._8_00(fourbitzero_1__8_00), ._8_75(fourbitzero_1__8_75));
  fourInverter fourinverter_1 (.in_1(mx2i_4_1_out_4), .out_2(_10_5[7:4]));
  not not_1 (_10_5_2, twoonetransmission_1_out_4);
  fourBitOne fourbitone_2 (.a(in_1[3:0]), .b(in_2[3:0]), ._8_00(fourbitone_2__8_00), ._8_75(_10_5[3:0]));

  // Notes on the sheet:
  //   8.00
  //   9.75
  //   8.75
  //   8.00
  //   9.75
  //   8.75
  //   10.5
  //   10.5
  //   8.00
  //   8.75
  //   Eight Bit Carry Select Adder
endmodule

module mx2i_8 (
  input  [7:0] in_1,
  input  [7:0] in_2,
  input  s,
  output [7:0] out_4
);

  mx2i_4 mx2i_4_1 (.in_2(in_2[3:0]), .in_1(in_1[3:0]), .s(s), .out_4(out_4[3:0]));
  mx2i_4 mx2i_4_2 (.in_2(in_2[7:4]), .in_1(in_1[7:4]), .s(s), .out_4(out_4[7:4]));
endmodule

module eightInverter (
  input  [7:0] in_1,
  output [7:0] out_2
);

  fourInverter fourinverter_1 (.in_1(in_1[3:0]), .out_2(out_2[3:0]));
  fourInverter fourinverter_2 (.in_1(in_1[7:4]), .out_2(out_2[7:4]));
endmodule

module eightBitCarryFull (
  input  [7:0] in_1,
  input  in_2,
  input  [7:0] in_3,
  output [7:0] _10_5,
  output _10_5_2
);

  wire fourbitfull_1__8_00, fourbitone_1__8_00, fourbitzero_1__8_00, twoonetransmission_1_out_4;
  wire [3:0] fourbitone_1__8_75, fourbitzero_1__8_75, mx2i_4_1_out_4;

  twoOneTransmission twoonetransmission_1 (
    .in_1(fourbitzero_1__8_00), .in_2(fourbitone_1__8_00), .in_3(fourbitfull_1__8_00),
    .out_4(twoonetransmission_1_out_4));
  fourBitOne fourbitone_1 (.a(in_1[7:4]), .b(in_3[7:4]), ._8_00(fourbitone_1__8_00), ._8_75(fourbitone_1__8_75));
  mx2i_4 mx2i_4_1 (
    .in_2(fourbitone_1__8_75), .in_1(fourbitzero_1__8_75), .s(fourbitfull_1__8_00), .out_4(mx2i_4_1_out_4));
  fourBitZero fourbitzero_1 (.a(in_1[7:4]), .b(in_3[7:4]), ._8_00(fourbitzero_1__8_00), ._8_75(fourbitzero_1__8_75));
  fourInverter fourinverter_1 (.in_1(mx2i_4_1_out_4), .out_2(_10_5[7:4]));
  not not_1 (_10_5_2, twoonetransmission_1_out_4);
  fourBitFull fourbitfull_1 (
    .a(in_1[3:0]), .b(in_3[3:0]), .in_2(in_2), ._8_00(fourbitfull_1__8_00), ._8_75(_10_5[3:0]));

  // Notes on the sheet:
  //   8.00
  //   9.75
  //   8.75
  //   8.00
  //   9.75
  //   8.75
  //   10.5
  //   10.5
  //   8.00
  //   8.75
  //   Eight Bit Carry Select Adder
endmodule

module sixteenBitCarryFull (
  input  [15:0] in_1,
  input  [15:0] in_2,
  input  in_3,
  output [15:0] _13,
  output _13_2
);

  wire eightbitcarry_1__10_5_2, eightbitcarryfull_1__10_5_2, eightbitcarryone_1__10_5_2,
       twoonetransmission_1_out_4;
  wire [7:0] eightbitcarry_1__10_5, eightbitcarryone_1__10_5, mx2i_8_1_out_4;

  eightBitCarryOne eightbitcarryone_1 (
    .in_2(in_2[15:8]), .in_1(in_1[15:8]), ._10_5(eightbitcarryone_1__10_5),
    ._10_5_2(eightbitcarryone_1__10_5_2));
  twoOneTransmission twoonetransmission_1 (
    .in_1(eightbitcarry_1__10_5_2), .in_2(eightbitcarryone_1__10_5_2), .in_3(eightbitcarryfull_1__10_5_2),
    .out_4(twoonetransmission_1_out_4));
  eightBitCarry eightbitcarry_1 (
    .in_2(in_2[15:8]), .in_1(in_1[15:8]), ._10_5(eightbitcarry_1__10_5), ._10_5_2(eightbitcarry_1__10_5_2));
  mx2i_8 mx2i_8_1 (
    .in_1(eightbitcarry_1__10_5), .in_2(eightbitcarryone_1__10_5), .s(eightbitcarryfull_1__10_5_2),
    .out_4(mx2i_8_1_out_4));
  not not_1 (_13_2, twoonetransmission_1_out_4);
  eightInverter eightinverter_1 (.in_1(mx2i_8_1_out_4), .out_2(_13[15:8]));
  eightBitCarryFull eightbitcarryfull_1 (
    .in_3(in_2[7:0]), .in_1(in_1[7:0]), .in_2(in_3), ._10_5(_13[7:0]), ._10_5_2(eightbitcarryfull_1__10_5_2));

  // Notes on the sheet:
  //   10.5
  //   10.5
  //   10.5
  //   12.25
  //   10.5
  //   12.25
  //   10.5
  //   13
  //   10.5
endmodule

module subtractorv2 (
  input  [15:0] in_1,
  input  [15:0] in_2,
  input  in_3,
  output [15:0] out_4,
  output out_5
);

  wire not_2_out, xor_1_out, xor_2_out;
  wire [15:0] multiplexer_1_out, not_1_out;

  assign not_1_out = ~in_2;  // NOT_Gate not_1, 16 bits wide
  Multiplexer #(.width(16)) multiplexer_1 (.in0(in_2), .in1(not_1_out), .out(multiplexer_1_out), .sel(in_3));
  sixteenBitCarryFull sixteenbitcarryfull_1 (
    .in_2(multiplexer_1_out), .in_1(in_1), .in_3(in_3), ._13(out_4));  // open: _13_2
  xor xor_1 (xor_1_out, out_4[15], in_1[15]);
  xor xor_2 (xor_2_out, in_1[15], multiplexer_1_out[15]);
  not not_2 (not_2_out, xor_2_out);
  and and_1 (out_5, xor_1_out, not_2_out);
endmodule

module r0r1 (
  input  in_1,
  input  in_2,
  input  [15:0] in_3
);

  wire clk;
  wire [15:0] R0_q, R1_q, subtractorv2_1_out_4;

  Clock clock_1 (.out(clk));
  Register #(.width(16)) R0 (.D(subtractorv2_1_out_4), .en(1'b1), .clk(clk), .Q(R0_q), .clr(in_1));
  Register #(.width(16)) R1 (.D(in_3), .en(1'b1), .clk(clk), .Q(R1_q), .clr(in_1));
  subtractorv2 subtractorv2_1 (.in_1(R0_q), .in_2(R1_q), .in_3(in_2), .out_4(subtractorv2_1_out_4));  // open: out_5

  // Other names for the same wires on the sheet: rst = in_1
endmodule

module testRegisters (
  input  in_1
);

  wire clk, not_1_out, not_2_out, not_3_out, ovrfl, register_1_q, regwe_1_r0, regwe_1_r1, regwe_1_r2,
       regwe_1_r3, sub;
  wire [1:0] Rd, Rs;
  wire [3:0] ram_1_dout;
  wire [5:0] programcounter_1_out_6;
  wire [15:0] R0, R1, R2, R3, srcsel_1_out_6, srcsel_2_out_6, subtractorv2_1_out_4;

  Clock clock_1 (.out(clk));
  Hex_Digit_Display hex_digit_display_1 (.value(R0[11:8]));  // open: dp
  Hex_Digit_Display hex_digit_display_2 (.value(R0[15:12]));  // open: dp
  programCounter programcounter_1 (.in_2(clk), .in_3(in_1), .out_6(programcounter_1_out_6));  // open: jmpn, set, jump
  Hex_Digit_Display hex_digit_display_3 (.value(R0[7:4]));  // open: dp
  Hex_Digit_Display hex_digit_display_4 (.value(R0[3:0]));  // open: dp
  RAM #(.addrWidth(6), .asyncread("true"), .trigger("falling")) ram_1 (
    .addr(programcounter_1_out_6), .we(1'b0), .oe(1'b1), .clk(clk), .dout({Rd, Rs, ram_1_dout}));  // open: din
  Hex_Digit_Display hex_digit_display_5 (.value(R1[15:12]));  // open: dp
  Hex_Digit_Display hex_digit_display_6 (.value(R1[11:8]));  // open: dp
  Hex_Digit_Display hex_digit_display_7 (.value(R1[7:4]));  // open: dp
  Hex_Digit_Display hex_digit_display_8 (.value(R1[3:0]));  // open: dp
  Hex_Digit_Display hex_digit_display_9 (.value(R2[15:12]));  // open: dp
  Hex_Digit_Display hex_digit_display_10 (.value(R2[11:8]));  // open: dp
  Hex_Digit_Display hex_digit_display_11 (.value(R2[7:4]));  // open: dp
  not not_1 (not_1_out, ram_1_dout[1]);
  not not_2 (not_2_out, ram_1_dout[2]);
  not not_3 (not_3_out, ram_1_dout[3]);
  srcSel srcsel_1 (.in_1(R0), .in_2(R1), .in_3(R2), .in_4(R3), .in_5(Rd), .out_6(srcsel_1_out_6));
  srcSel srcsel_2 (.in_1(R0), .in_2(R1), .in_3(R2), .in_4(R3), .in_5(Rs), .out_6(srcsel_2_out_6));
  Hex_Digit_Display hex_digit_display_12 (.value(R2[3:0]));  // open: dp
  and and_1 (sub, ram_1_dout[0], not_1_out, not_2_out, not_3_out);
  Hex_Digit_Display hex_digit_display_13 (.value(R3[15:12]));  // open: dp
  Hex_Digit_Display hex_digit_display_14 (.value(R3[11:8]));  // open: dp
  Hex_Digit_Display hex_digit_display_15 (.value(R3[7:4]));  // open: dp
  Hex_Digit_Display hex_digit_display_16 (.value(R3[3:0]));  // open: dp
  subtractorv2 subtractorv2_1 (
    .in_1(srcsel_1_out_6), .in_2(srcsel_2_out_6), .in_3(sub), .out_4(subtractorv2_1_out_4), .out_5(ovrfl));
  regWE regwe_1 (.Rd(1'b1), .regWrite(Rd), .R0(regwe_1_r0), .R1(regwe_1_r1), .R2(regwe_1_r2), .R3(regwe_1_r3));
  Register #(.width(1)) register_1 (.D(1'b1), .en(ovrfl), .clk(clk), .Q(register_1_q), .clr(in_1));
  LED led_1 (.in(register_1_q));
  Register #(.width(16)) u_R0 (.D(subtractorv2_1_out_4), .en(regwe_1_r0), .clk(clk), .Q(R0), .clr(in_1));
  Register #(.width(16)) u_R1 (.D(subtractorv2_1_out_4), .en(regwe_1_r1), .clk(clk), .Q(R1), .clr(in_1));
  Register #(.width(16)) u_R2 (.D(subtractorv2_1_out_4), .en(regwe_1_r2), .clk(clk), .Q(R2), .clr(in_1));
  Register #(.width(16)) u_R3 (.D(subtractorv2_1_out_4), .en(regwe_1_r3), .clk(clk), .Q(R3), .clr(in_1));

  // Other names for the same wires on the sheet: rst = in_1

  // Notes on the sheet:
  //   4C 41 53 41 7B 43 53 7D
  //   0000 = add
  //   0001 = sub
  //   10 11 0001 = b1
  //   01 00 0001 = 41
  //   11 10 0000 = e0
  //   00 11 0000 = 30
  //   10 00 0000 = 80
endmodule

module regWE (
  input  Rd,
  input  [1:0] regWrite,
  output R0,
  output R1,
  output R2,
  output R3
);

  wire not_1_out, not_2_out, not_3_out, not_4_out;

  not not_1 (not_1_out, regWrite[1]);
  not not_2 (not_2_out, regWrite[0]);
  and and_1 (R0, Rd, not_2_out, not_3_out);
  not not_3 (not_3_out, regWrite[1]);
  and and_2 (R1, Rd, regWrite[0], not_1_out);
  not not_4 (not_4_out, regWrite[0]);
  and and_3 (R2, Rd, not_4_out, regWrite[1]);
  and and_4 (R3, Rd, regWrite[0], regWrite[1]);
endmodule

module srcSel (
  input  [15:0] in_1,
  input  [15:0] in_2,
  input  [15:0] in_3,
  input  [15:0] in_4,
  input  [1:0] in_5,
  output [15:0] out_6
);

  Multiplexer #(.select(2), .width(16)) multiplexer_1 (
    .in0(in_1), .in1(in_2), .in2(in_3), .in3(in_4), .out(out_6), .sel(in_5));
endmodule

module programCounter (
  input  [5:0] set,
  input  in_2,
  input  in_3,
  input  jmpn,
  input  jump,
  output [5:0] out_6
);

  wire or_1_out;
  wire [5:0] adder_1_out, multiplexer_1_out;

  or or_1 (or_1_out, jmpn, jump);
  Multiplexer #(.width(6)) multiplexer_1 (.in0(adder_1_out), .in1(set), .out(multiplexer_1_out), .sel(or_1_out));
  Register #(.width(6)) register_1 (.D(multiplexer_1_out), .en(1'b1), .clk(in_2), .Q(out_6), .clr(in_3));
  Adder #(.width(6)) adder_1 (.a(out_6), .b(6'b000001), .out(adder_1_out));  // open: cin, cout
endmodule

module firstProgramV2 (
  input  in_1,
  output [15:0] out_2
);

  wire and_2_out, clk, halt, jump, jumpn, not_1_out, not_2_out, not_3_out, ovrfl, register_3_q, regwe_1_r0,
       regwe_1_r1, regwe_1_r2, regwe_1_r3, sub, we, writeToReg;
  wire [1:0] ldI, Rd;
  wire [3:0] instruction, register_1_q, register_1_q_2, register_2_q, register_2_q_2;
  wire [5:0] programcounter_1_out_6, targPC;
  wire [7:0] debugging, pc;
  wire [15:0] decoded, load, move, multiplexer_1_out, multiplexer_2_out, R0, R1, R2, R3, srcsel_1_out_6,
       srcsel_2_out_6, srcsel_4_out_6, srcsel_5_out_6, sum;

  Clock clock_1 (.out(clk));
  Hex_Digit_Display hex_digit_display_1 (.value(pc[7:4]));  // open: dp
  Hex_Digit_Display hex_digit_display_2 (.value(R0[11:8]));  // open: dp
  Hex_Digit_Display hex_digit_display_3 (.value(R0[15:12]));  // open: dp
  programCounter programcounter_1 (
    .jmpn(jumpn), .set(targPC), .jump(jump), .in_2(clk), .in_3(in_1), .out_6(programcounter_1_out_6));
  Hex_Digit_Display hex_digit_display_4 (.value(debugging[7:4]));  // open: dp
  Hex_Digit_Display hex_digit_display_5 (.value(pc[3:0]));  // open: dp
  srcSel srcsel_1 (.in_1(R0), .in_2(R1), .in_3(R2), .in_4(R3), .in_5(ldI), .out_6(srcsel_1_out_6));
  srcSel srcsel_2 (.in_1(R0), .in_2(R1), .in_3(R2), .in_4(R3), .in_5(Rd), .out_6(srcsel_2_out_6));
  not not_1 (not_1_out, instruction[2]);
  srcSel srcsel_3 (.in_1(R0), .in_2(R1), .in_3(R2), .in_4(R3), .in_5(ldI), .out_6(move));
  Hex_Digit_Display hex_digit_display_6 (.value(R0[7:4]));  // open: dp
  Hex_Digit_Display hex_digit_display_7 (.value(R0[3:0]));  // open: dp
  RAM #(.addrWidth(6), .asyncread("true"), .trigger("falling")) ram_1 (
    .addr(programcounter_1_out_6), .we(1'b0), .oe(1'b1), .clk(clk), .dout(pc));  // open: din
  Hex_Digit_Display hex_digit_display_8 (.value(debugging[3:0]));  // open: dp
  Register register_1 (.D(debugging), .en(1'b1), .clk(clk), .Q({register_1_q_2, register_1_q}), .clr(in_1));
  not not_2 (not_2_out, we);
  and and_1 (we, instruction[0], instruction[1], not_1_out, instruction[3]);
  Hex_Digit_Display hex_digit_display_9 (.value(R1[15:12]));  // open: dp
  Hex_Digit_Display hex_digit_display_10 (.value(register_1_q_2));  // open: dp
  Hex_Digit_Display hex_digit_display_11 (.value(register_1_q));  // open: dp
  RAM #(.asyncread("true"), .dataWidth(16), .trigger("falling")) dataMemory (
    .addr(srcsel_1_out_6[7:0]), .we(we), .oe(not_2_out), .clk(clk), .din(srcsel_2_out_6), .dout(load));
  Hex_Digit_Display hex_digit_display_12 (.value(R1[11:8]));  // open: dp
  Hex_Digit_Display hex_digit_display_13 (.value(R1[7:4]));  // open: dp
  Register register_2 (
    .D({register_1_q_2, register_1_q}), .en(1'b1), .clk(clk), .Q({register_2_q_2, register_2_q}), .clr(in_1));
  Hex_Digit_Display hex_digit_display_14 (.value(R1[3:0]));  // open: dp
  Register instructionRegister (.D(pc), .en(1'b1), .clk(clk), .Q(debugging), .clr(in_1));
  Hex_Digit_Display hex_digit_display_15 (.value(register_2_q_2));  // open: dp
  Hex_Digit_Display hex_digit_display_16 (.value(register_2_q));  // open: dp
  Hex_Digit_Display hex_digit_display_17 (.value(R2[15:12]));  // open: dp
  Hex_Digit_Display hex_digit_display_18 (.value(R2[11:8]));  // open: dp
  Hex_Digit_Display hex_digit_display_19 (.value(R2[7:4]));  // open: dp
  srcSel srcsel_4 (.in_1(R0), .in_2(R1), .in_3(R2), .in_4(R3), .in_5(Rd), .out_6(srcsel_4_out_6));
  srcSel srcsel_5 (.in_1(R0), .in_2(R1), .in_3(R2), .in_4(R3), .in_5(ldI), .out_6(srcsel_5_out_6));
  Hex_Digit_Display hex_digit_display_20 (.value(R2[3:0]));  // open: dp
  Hex_Digit_Display hex_digit_display_21 (.value(R3[15:12]));  // open: dp
  Hex_Digit_Display hex_digit_display_22 (.value(R3[11:8]));  // open: dp
  subtractorv2 subtractorv2_1 (.in_1(srcsel_4_out_6), .in_2(srcsel_5_out_6), .in_3(sub), .out_4(sum), .out_5(ovrfl));
  not not_3 (not_3_out, halt);
  Multiplexer #(.width(16)) multiplexer_1 (.in0(sum), .in1(move), .out(multiplexer_1_out), .sel(instruction[2]));
  Multiplexer #(.width(16)) multiplexer_2 (
    .in0({{14{1'b0}}, ldI}), .in1(load), .out(multiplexer_2_out), .sel(instruction[0]));
  Hex_Digit_Display hex_digit_display_23 (.value(R3[7:4]));  // open: dp
  Hex_Digit_Display hex_digit_display_24 (.value(R3[3:0]));  // open: dp
  irDecoder irdecoder_1 (
    .IR(debugging), .clk(clk), .rst(in_1), .neg(sum[15]), .sub(sub), .Rs(ldI), .Rd(Rd),
    .instruction(instruction), .writeToReg(writeToReg), .targetPC(targPC), .jump(jump), .jumpn(jumpn),
    .halt(halt));
  Hex_Digit_Display hex_digit_display_25 (.value(sum[15:12]));  // open: dp
  Hex_Digit_Display hex_digit_display_26 (.value(sum[11:8]));  // open: dp
  and and_2 (and_2_out, writeToReg, not_3_out);
  cycleCounter cyclecounter_1 (.halt(halt), .clk(clk), .rst(in_1), .cycles(out_2));
  Hex_Digit_Display hex_digit_display_27 (.value(sum[7:4]));  // open: dp
  Hex_Digit_Display hex_digit_display_28 (.value(sum[3:0]));  // open: dp
  regWE regwe_1 (.Rd(and_2_out), .regWrite(Rd), .R0(regwe_1_r0), .R1(regwe_1_r1), .R2(regwe_1_r2), .R3(regwe_1_r3));
  Multiplexer #(.width(16)) multiplexer_3 (
    .in0(multiplexer_1_out), .in1(multiplexer_2_out), .out(decoded), .sel(instruction[3]));
  Register #(.width(1)) register_3 (.D(writeToReg), .en(ovrfl), .clk(clk), .Q(register_3_q), .clr(in_1));
  LED led_1 (.in(register_3_q));
  Register #(.width(16)) u_R0 (.D(decoded), .en(regwe_1_r0), .clk(clk), .Q(R0), .clr(in_1));
  Register #(.width(16)) u_R1 (.D(decoded), .en(regwe_1_r1), .clk(clk), .Q(R1), .clr(in_1));
  Register #(.width(16)) u_R2 (.D(decoded), .en(regwe_1_r2), .clk(clk), .Q(R2), .clr(in_1));
  Register #(.width(16)) u_R3 (.D(decoded), .en(regwe_1_r3), .clk(clk), .Q(R3), .clr(in_1));

  // Other names for the same wires on the sheet: Rs[1:0] = ldI; rst = in_1

  // Notes on the sheet:
  //   fetch
  //   decode
  //   execute
  //   writeback
  //   100 numbers [8,6b]
  //   rslt
  //   4C 41 53 41 7B 43 53 7D
  //   10 11 0001 = b1
  //   01 00 0001 = 41
  //   11 10 0000 = e0
  //   00 11 0000 = 30
  //   10 00 0000 = 80
endmodule

module irDecoder (
  input  [7:0] IR,
  input  clk,
  input  rst,
  input  neg,
  output sub,
  output [1:0] Rs,
  output [1:0] Rd,
  output [3:0] instruction,
  output writeToReg,
  output [5:0] targetPC,
  output jump,
  output jumpn,
  output halt
);

  wire and_1_out, and_2_out, and_3_out, and_6_out, fv, nor_1_out, nor_2_out, nor_3_out, not_1_out, not_2_out,
       not_3_out, not_4_out, not_5_out, not_6_out, not_7_out;

  not not_1 (not_1_out, IR[0]);
  and and_1 (and_1_out, IR[0], IR[1], not_2_out, IR[3]);
  not not_2 (not_2_out, IR[2]);
  nor nor_1 (nor_1_out, IR[0], IR[1], IR[2], IR[3], IR[4], IR[5], IR[6], IR[7]);
  nor nor_2 (nor_2_out, IR[0], IR[1]);
  not not_3 (not_3_out, IR[1]);
  not not_4 (not_4_out, IR[3]);
  and and_2 (and_2_out, not_1_out, IR[1], IR[2], not_4_out, IR[4], IR[5], IR[6], IR[7]);
  and and_3 (and_3_out, IR[0], IR[1], not_5_out, not_6_out);
  not not_5 (not_5_out, IR[2]);
  not not_6 (not_6_out, IR[3]);
  and and_4 (jumpn, IR[0], not_3_out, neg, fv);
  Register #(.width(1)) register_1 (.D(and_3_out), .en(1'b1), .clk(clk), .Q(sub), .clr(rst));
  Register #(.width(2)) register_2 (.D(IR[5:4]), .en(1'b1), .clk(clk), .Q(Rs), .clr(rst));
  Register #(.width(2)) register_3 (.D(IR[7:6]), .en(1'b1), .clk(clk), .Q(Rd), .clr(rst));
  Register #(.width(4)) register_4 (.D(IR[3:0]), .en(1'b1), .clk(clk), .Q(instruction), .clr(rst));
  nor nor_3 (nor_3_out, and_1_out, nor_1_out, and_6_out, nor_2_out);
  and and_5 (jump, fv, nor_2_out);
  and and_6 (and_6_out, not_7_out, IR[0]);
  not not_7 (not_7_out, IR[1]);
  Register #(.width(1)) register_5 (.D(and_2_out), .en(1'b1), .clk(clk), .Q(halt), .clr(rst));
  Register #(.width(1)) register_6 (.D(nor_3_out), .en(1'b1), .clk(clk), .Q(writeToReg), .clr(rst));
  D_Flip_Flop d_ff_1 (.D(1'b1), .clk(clk), .Q(fv), .reset(rst));  // open: Qn, preset

  assign targetPC = IR[7:2];

  // Other names for the same wires on the sheet: zeroThree[3:0] = IR[3:0]

  // Notes on the sheet:
  //   if any input into last nor gate is 1, then writeToReg will be zero
endmodule

module cycleCounter (
  input  halt,
  input  clk,
  input  rst,
  output [15:0] cycles
);

  wire not_1_out, register_1_q;
  wire [15:0] adder_1_out;

  Register #(.width(1)) register_1 (.D(1'b1), .en(halt), .clk(clk), .Q(register_1_q), .clr(rst));
  Adder #(.width(16)) adder_1 (.a(cycles), .b(16'h1), .out(adder_1_out));  // open: cin, cout
  Register #(.width(16)) register_2 (.D(adder_1_out), .en(not_1_out), .clk(clk), .Q(cycles), .clr(rst));
  not not_1 (not_1_out, register_1_q);
endmodule
