// Logisim project eightBitAdder.circ as structural Verilog: 4 circuits, main circuit fourBitZero
module fourBitZero (
  input  [3:0] a,
  input  [3:0] b,
  output [3:0] _8_75,
  output _8_00
);

  wire fa0_1_cout, faopt1_2_cout, faopt2_1_cout;

  FAopt1 faopt1_1 (.a(b[3]), .b(a[3]), .cin(faopt1_2_cout), .sum(_8_75[3]), .cout(_8_00));
  FAopt1 faopt1_2 (.a(b[2]), .b(a[2]), .cin(faopt2_1_cout), .sum(_8_75[2]), .cout(faopt1_2_cout));
  FAopt2 faopt2_1 (.b(b[1]), .c(fa0_1_cout), .a(a[1]), .sum(_8_75[1]), .cout(faopt2_1_cout));
  FA0 fa0_1 (.in1(a[0]), .in2(b[0]), .sum(_8_75[0]), .cout(fa0_1_cout));

  // Notes on the sheet:
  //   8.00
  //   8.75
  //   6.00
  //   6.75
  //   4.00
  //   1.75
  //   5.5
  //   2.75
endmodule

module eightBit (
  input  [7:0] a,
  input  [7:0] b,
  output [7:0] out_3,
  output out_4
);

  wire faopt1_2_cout, faopt1_3_cout, faopt1_4_cout, faopt1_5_cout, faopt1_6_cout, faopt2_1_p2, faopt2_1_p5;

  FAopt1 faopt1_1 (.a(b[7]), .b(a[7]), .cin(faopt1_2_cout), .sum(out_3[7]), .cout(out_4));
  FAopt1 faopt1_2 (.a(b[6]), .b(a[6]), .cin(faopt1_3_cout), .sum(out_3[6]), .cout(faopt1_2_cout));
  FAopt1 faopt1_3 (.a(b[5]), .b(a[5]), .cin(faopt1_4_cout), .sum(out_3[5]), .cout(faopt1_3_cout));
  FAopt1 faopt1_4 (.a(b[4]), .b(a[4]), .cin(faopt1_5_cout), .sum(out_3[4]), .cout(faopt1_4_cout));
  FAopt1 faopt1_5 (.a(b[3]), .b(a[3]), .cin(faopt1_6_cout), .sum(out_3[3]), .cout(faopt1_5_cout));
  FAopt1 faopt1_6 (.a(b[2]), .b(a[2]), .cin(faopt2_1_p2), .sum(out_3[2]), .cout(faopt1_6_cout));
  // FAopt2 faopt2_1: pin names not known; wires that end beside it: b[1], faopt2_1_p2, a[1], out_3[1], faopt2_1_p5
  FA0 fa0_1 (.in1(a[0]), .in2(b[0]), .sum(out_3[0]), .cout(faopt2_1_p5));

  // Notes on the sheet:
  //   1.75
  //   2.75
endmodule

module fourBitOne (
  input  [3:0] a,
  input  [3:0] b,
  output [3:0] _8_75,
  output _8_00
);

  wire fa1_1_cout, faopt1_2_cout, faopt2_1_cout;

  FAopt1 faopt1_1 (.a(b[3]), .b(a[3]), .cin(faopt1_2_cout), .sum(_8_75[3]), .cout(_8_00));
  FAopt1 faopt1_2 (.a(b[2]), .b(a[2]), .cin(faopt2_1_cout), .sum(_8_75[2]), .cout(faopt1_2_cout));
  FAopt2 faopt2_1 (.b(b[1]), .c(fa1_1_cout), .a(a[1]), .sum(_8_75[1]), .cout(faopt2_1_cout));
  FA1 fa1_1 (.in1(a[0]), .in2(b[0]), .sum(_8_75[0]), .cout(fa1_1_cout));

  // Notes on the sheet:
  //   8.00
  //   8.75
  //   6.00
  //   6.75
  //   4.00
  //   1.75
  //   5.5
  //   2.75
endmodule

module fourBitFull (
  input  [3:0] a,
  input  in_2,
  input  [3:0] b,
  output [3:0] _8_75,
  output _8_00
);

  wire faopt1_2_cout, faopt2_1_cout, faopt2_2_cout;

  FAopt1 faopt1_1 (.a(b[3]), .b(a[3]), .cin(faopt1_2_cout), .sum(_8_75[3]), .cout(_8_00));
  FAopt1 faopt1_2 (.a(b[2]), .b(a[2]), .cin(faopt2_1_cout), .sum(_8_75[2]), .cout(faopt1_2_cout));
  FAopt2 faopt2_1 (.b(b[1]), .c(faopt2_2_cout), .a(a[1]), .sum(_8_75[1]), .cout(faopt2_1_cout));
  FAopt2 faopt2_2 (.b(b[0]), .c(in_2), .a(a[0]), .sum(_8_75[0]), .cout(faopt2_2_cout));

  // Notes on the sheet:
  //   8.00
  //   8.75
  //   6.00
  //   6.75
  //   4.00
  //   1.75
  //   5.5
  //   2.75
endmodule
