// Logisim project halfAdder2.circ as structural Verilog: 2 circuits, main circuit FA1
module FA1 (
  input  in1,
  input  in2,
  output sum,
  output cout
);

  wire nand_1_out;

  or or_1 (cout, in1, in2);
  nand nand_1 (nand_1_out, in2, in1);
  nand nand_2 (sum, cout, nand_1_out);

  // Notes on the sheet:
  //   14 Transistors
  //   FA1
  //   Nikhil Jayakumar
  //   2.75
  //   1.75
endmodule

module FA0 (
  input  in1,
  input  in2,
  output sum,
  output cout
);

  wire nor_1_out;

  nor nor_1 (nor_1_out, in1, in2);
  and and_1 (cout, in2, in1);
  nor nor_2 (sum, nor_1_out, cout);

  // Notes on the sheet:
  //   14 transistors
  //   FA0
  //   Nikhil Jayakumar
  //   sum
  //   2.75
  //   1.75
endmodule
