// Logisim project mux.circ as structural Verilog: 4 circuits, main circuit twoOne
module twoOne (
  input  in_1,
  input  s,
  input  in_3,
  output out_4
);

  wire nand_1_out, nand_2_out, not_1_out;

  not not_1 (not_1_out, s);
  nand nand_1 (nand_1_out, in_1, not_1_out);
  nand nand_2 (nand_2_out, s, in_3);
  nand nand_3 (out_4, nand_1_out, nand_2_out);

  // Notes on the sheet:
  //   max(s+2.75,in0+2,in1+2)
endmodule

module twoOneTransmission (
  input  in_1,
  input  in_2,
  input  in_3,
  output out_4
);

  wire not_1_out, transmission_1_p4;

  not not_1 (not_1_out, in_3);
  // Transmission_Gate transmission_1: pin names not known; wires that end beside it: in_1, in_3, not_1_out, transmission_1_p4
  // Transmission_Gate transmission_2: pin names not known; wires that end beside it: in_2, not_1_out, in_3, transmission_1_p4
  not not_2 (out_4, transmission_1_p4);

  // Notes on the sheet:
  //   8 transistors
  //   max(s+1.75,in0+1,in1+1)
  //   Nikhil Jayakumar
endmodule

module fourOneTransmission (
  input  in_1,
  input  in_2,
  input  in_3,
  input  in_4,
  input  s1,
  input  s0,
  output out_7
);

  wire twoonetransmission_1_out_4, twoonetransmission_2_out_4;

  twoOneTransmission twoonetransmission_1 (.in_1(in_1), .in_2(in_2), .in_3(s0), .out_4(twoonetransmission_1_out_4));
  twoOneTransmission twoonetransmission_2 (.in_1(in_3), .in_2(in_4), .in_3(s0), .out_4(twoonetransmission_2_out_4));
  twoOneTransmission twoonetransmission_3 (
    .in_1(twoonetransmission_1_out_4), .in_2(twoonetransmission_2_out_4), .in_3(s1), .out_4(out_7));

  // Notes on the sheet:
  //   24 Transistors
  //   Nikhil Jayakumar
  //    max(s0+2.75, s1+1.75, in0+2, in1+2, in2+2, in3+2)
endmodule

module fourOne (
  input  in0,
  input  in1,
  input  in2,
  input  in3,
  input  s0,
  input  s1,
  output out_7
);

  wire twoone_1_out_4, twoone_2_out_4;

  twoOne twoone_1 (.s(s0), .in_3(in1), .in_1(in0), .out_4(twoone_1_out_4));
  twoOne twoone_2 (.s(s0), .in_3(in3), .in_1(in2), .out_4(twoone_2_out_4));
  twoOne twoone_3 (.s(s1), .in_3(twoone_2_out_4), .in_1(twoone_1_out_4), .out_4(out_7));

  // Notes on the sheet:
  //   42 Transistors
  //   Nikhil Jayakumar
  //    max(s0+4.75, s1+2.75, in0+4, in1+4, in2+4, in3+4)
endmodule
