// Logisim project optimization.circ as structural Verilog: 2 circuits, main circuit FAopt1
module FAopt1 (
  input  a,
  input  b,
  input  cin,
  output sum,
  output cout
);

  wire nand_1_out, nand_2_out, nor_1_out, nor_2_out, nor_3_out, not_1_out, not_2_out;

  nor nor_1 (nor_1_out, a, b);
  nand nand_1 (nand_1_out, a, b);
  not not_1 (not_1_out, nand_1_out);
  nor nor_2 (nor_2_out, nor_1_out, not_1_out);
  nand nand_2 (nand_2_out, nor_2_out, cin);
  nor nor_3 (nor_3_out, nor_2_out, cin);
  not not_2 (not_2_out, nand_2_out);
  nor nor_4 (sum, nor_3_out, not_2_out);
  nand nand_3 (cout, nand_2_out, nand_1_out);

  // Notes on the sheet:
  //   32 Transistors
  //   FAopt1
  //   Nikhil Jayakumar
  //   if cin < 2.75: 5.5
  //   else: cin+2.75
  //   if cin < 2.75: 4.75
  //   else: cin+2
endmodule

module FAopt2 (
  input  a,
  input  b,
  input  c,
  output sum,
  output cout
);

  wire and_1_out, nand_1_out, nand_2_out, nand_3_out, nor_1_out, nor_2_out, nor_3_out, not_1_out;

  nor nor_1 (nor_1_out, a, b);
  nand nand_1 (nand_1_out, b, a);
  nor nor_2 (nor_2_out, nor_1_out, not_1_out);
  not not_1 (not_1_out, nand_1_out);
  nand nand_2 (nand_2_out, b, c);
  nand nand_3 (nand_3_out, c, a);
  nand nand_4 (cout, nand_1_out, nand_2_out, nand_3_out);
  nor nor_3 (nor_3_out, nor_2_out, c);
  and and_1 (and_1_out, nor_2_out, c);
  nor nor_4 (sum, nor_3_out, and_1_out);

  // Notes on the sheet:
  //   42 Transistors
  //   FAopt2
  //   Nikhil Jayakumar
  //   else: cin+2.75
  //   cin+2.25
  //   if cin < 2.75: 5.50
endmodule
