// Logisim project subtractor.circ as structural Verilog: 1 circuit, main circuit v1
module v1 (
  input  [15:0] in_1,
  input  [15:0] in_2,
  input  OP,
  output [15:0] out_4,
  output out_5
);

  wire not_2_out, xor_1_out, xor_2_out;
  wire [15:0] multiplexer_1_out, not_1_out;

  Multiplexer #(.width(16)) multiplexer_1 (.in0(in_2), .in1(not_1_out), .out(multiplexer_1_out), .sel(OP));
  assign not_1_out = ~in_2;  // NOT_Gate not_1, 16 bits wide
  Adder #(.width(16)) adder_1 (.a(in_1), .b(multiplexer_1_out), .out(out_4), .cin(OP));  // open: cout
  xor xor_1 (xor_1_out, out_4[15], multiplexer_1_out[15]);
  xor xor_2 (xor_2_out, multiplexer_1_out[15], in_1[15]);
  not not_2 (not_2_out, xor_2_out);
  and and_1 (out_5, xor_1_out, not_2_out);
endmodule
